// Digital circuit 02-02.dig as structural Verilog
module _02_02 (
  input  A,
  input  B,
  output Output
);

  wire A__plus_B, A_plus_B, not_1_out, not_2_out;

  not not_1 (not_1_out, A);
  not not_2 (not_2_out, B);
  or or_1 (A__plus_B, not_1_out, not_2_out);
  and and_1 (Output, A_plus_B, A__plus_B);
  or or_2 (A_plus_B, A, B);
endmodule
