// Digital circuit 2564_1.dig as structural Verilog
module _2564_1 (
  input  [2:0] B,
  input  [2:0] A
);

  wire add_1_c_o, add_2_c_o, comparator_1_eq, comparator_1_gt, comparator_1_lt, or_1_out;
  wire [3:0] add_1_s;

  Add add_1 (.a(A[0]), .b(B[0]), .c_i(1'b0), .s(add_1_s[0]), .c_o(add_1_c_o));
  Add add_2 (.a(A[1]), .b(B[1]), .c_i(add_1_c_o), .s(add_1_s[1]), .c_o(add_2_c_o));
  Add add_3 (.a(A[2]), .b(B[2]), .c_i(add_2_c_o), .s(add_1_s[2]), .c_o(add_1_s[3]));
  Seven_Seg seven_seg_1 (
    .a(or_1_out), .b(1'b1), .c(1'b1), .d(or_1_out), .e(or_1_out), .f(or_1_out), .g(1'b0), .dp(1'b1));
  or or_1 (or_1_out, comparator_1_eq, comparator_1_lt);
  Comparator #(.Bits(4)) comparator_1 (
    .a(add_1_s), .b(4'b0111), .gt(comparator_1_gt), .eq(comparator_1_eq), .lt(comparator_1_lt));
endmodule
