// Digital circuit 2564_1_Best.dig as structural Verilog
module _2564_1_Best (
  input  [2:0] B,
  input  [2:0] A
);

  wire comparator_1_eq, comparator_1_gt, comparator_1_lt, or_1_out;
  wire [2:0] add_1_s;
  wire [3:3] add_1_c_o;

  Add #(.Bits(3)) add_1 (.a(A), .b(B), .c_i(1'b0), .s(add_1_s), .c_o(add_1_c_o[3]));
  Seven_Seg seven_seg_1 (
    .a(or_1_out), .b(1'b1), .c(1'b1), .d(or_1_out), .e(or_1_out), .f(or_1_out), .g(1'b0), .dp(1'b1));
  or or_1 (or_1_out, comparator_1_eq, comparator_1_lt);
  Comparator #(.Bits(4)) comparator_1 (
    .a({add_1_c_o[3], add_1_s}), .b(4'b0111), .gt(comparator_1_gt), .eq(comparator_1_eq), .lt(comparator_1_lt));
endmodule
