// Digital circuit 2566_01.dig as structural Verilog
module _2566_01 (
  input  [3:0] In,
  output Y
);

  wire and_1_out, and_2_out, and_3_out, and_4_out, not_1_out, not_2_out, not_3_out, not_4_out;

  not not_1 (not_1_out, In[3]);
  not not_2 (not_2_out, In[2]);
  not not_3 (not_3_out, In[1]);
  not not_4 (not_4_out, In[0]);
  and and_1 (and_1_out, not_1_out, not_2_out, In[0]);
  and and_2 (and_2_out, not_1_out, In[2], not_3_out);
  and and_3 (and_3_out, In[3], In[1], not_4_out);
  and and_4 (and_4_out, not_3_out, In[0]);
  or or_1 (Y, and_1_out, and_2_out, and_3_out, and_4_out);
endmodule
