// Digital circuit 01-Counter.dig as structural Verilog
module _01_Counter (
  input  clk,
  input  reset,
  output A,
  output B,
  output C,
  output [2:0] Total
);

  wire and_1_out, and_2_out, and_3_out, and_4_out, and_5_out, and_6_out, and_7_out, and_8_out, D0, D1, D2;

  and and_1 (and_1_out, B, ~A, ~reset);  // And
  and and_2 (and_2_out, ~C, B, ~reset);  // And
  and and_3 (and_3_out, C, ~B, A, ~reset);  // And
  and and_4 (and_4_out, ~C, ~B, ~reset);  // And
  and and_5 (and_5_out, ~C, A, ~reset);  // And
  and and_6 (and_6_out, ~B, A, ~reset);  // And
  and and_7 (and_7_out, C, ~A, ~reset);  // And
  and and_8 (and_8_out, ~B, A, ~reset);  // And
  D_FF d_ff_1 (.D(D0), .C(clk), .Q(A));  // open: nQ
  or or_1 (D2, and_1_out, and_2_out, and_3_out);
  or or_2 (D1, and_4_out, and_5_out, and_6_out);
  or or_3 (D0, and_7_out, and_8_out);
  D_FF d_ff_2 (.D(D1), .C(clk), .Q(B));  // open: nQ
  D_FF d_ff_3 (.D(D2), .C(clk), .Q(C));  // open: nQ

  assign Total = {C, B, A};

  // Other names for the same wires on the sheet: Q0 = A; Q1 = B; Q2 = C
endmodule
