// Digital circuit 03-Second Largest_Send.dig as structural Verilog
module _03_Second_Largest_Send (
  input  \input ,
  input  reset,
  input  clk,
  input  [15:0] A,
  output [15:0] second
);

  wire and_1_out, and_2_out, and_3_out, comparator_1_gt, comparator_2_gt;
  wire [15:0] Max, multiplexer_1_out, multiplexer_2_out, multiplexer_3_out, multiplexer_4_out,
       multiplexer_5_out;

  Comparator #(.Bits(16)) comparator_1 (.a(A), .b(Max), .gt(comparator_1_gt));  // open: eq, lt
  D_FF d_ff_1 (.D(multiplexer_1_out[15]), .C(clk), .Q(Max[15]));  // open: nQ
  D_FF d_ff_2 (.D(multiplexer_1_out[14]), .C(clk), .Q(Max[14]));  // open: nQ
  D_FF d_ff_3 (.D(multiplexer_1_out[13]), .C(clk), .Q(Max[13]));  // open: nQ
  D_FF d_ff_4 (.D(multiplexer_1_out[12]), .C(clk), .Q(Max[12]));  // open: nQ
  and and_1 (and_1_out, comparator_1_gt, \input );
  D_FF d_ff_5 (.D(multiplexer_1_out[11]), .C(clk), .Q(Max[11]));  // open: nQ
  D_FF d_ff_6 (.D(multiplexer_1_out[10]), .C(clk), .Q(Max[10]));  // open: nQ
  D_FF d_ff_7 (.D(multiplexer_1_out[9]), .C(clk), .Q(Max[9]));  // open: nQ
  D_FF d_ff_8 (.D(multiplexer_1_out[8]), .C(clk), .Q(Max[8]));  // open: nQ
  D_FF d_ff_9 (.D(multiplexer_1_out[7]), .C(clk), .Q(Max[7]));  // open: nQ
  D_FF d_ff_10 (.D(multiplexer_1_out[6]), .C(clk), .Q(Max[6]));  // open: nQ
  Multiplexer #(.Bits(16)) multiplexer_1 (
    .sel(reset), .in_0(multiplexer_2_out), .in_1({16{1'b0}}), .out(multiplexer_1_out));
  D_FF d_ff_11 (.D(multiplexer_1_out[5]), .C(clk), .Q(Max[5]));  // open: nQ
  D_FF d_ff_12 (.D(multiplexer_1_out[4]), .C(clk), .Q(Max[4]));  // open: nQ
  Multiplexer #(.Bits(16)) multiplexer_2 (.sel(and_1_out), .in_0(Max), .in_1(A), .out(multiplexer_2_out));
  D_FF d_ff_13 (.D(multiplexer_1_out[3]), .C(clk), .Q(Max[3]));  // open: nQ
  D_FF d_ff_14 (.D(multiplexer_1_out[2]), .C(clk), .Q(Max[2]));  // open: nQ
  D_FF d_ff_15 (.D(multiplexer_1_out[1]), .C(clk), .Q(Max[1]));  // open: nQ
  D_FF d_ff_16 (.D(multiplexer_1_out[0]), .C(clk), .Q(Max[0]));  // open: nQ
  D_FF d_ff_17 (.D(multiplexer_5_out[15]), .C(clk), .Q(second[15]));  // open: nQ
  D_FF d_ff_18 (.D(multiplexer_5_out[14]), .C(clk), .Q(second[14]));  // open: nQ
  D_FF d_ff_19 (.D(multiplexer_5_out[13]), .C(clk), .Q(second[13]));  // open: nQ
  Comparator #(.Bits(16)) comparator_2 (.a(A), .b(second), .gt(comparator_2_gt));  // open: eq, lt
  D_FF d_ff_20 (.D(multiplexer_5_out[12]), .C(clk), .Q(second[12]));  // open: nQ
  D_FF d_ff_21 (.D(multiplexer_5_out[11]), .C(clk), .Q(second[11]));  // open: nQ
  D_FF d_ff_22 (.D(multiplexer_5_out[10]), .C(clk), .Q(second[10]));  // open: nQ
  D_FF d_ff_23 (.D(multiplexer_5_out[9]), .C(clk), .Q(second[9]));  // open: nQ
  and and_2 (and_2_out, comparator_2_gt, ~comparator_1_gt, \input );  // And
  and and_3 (and_3_out, comparator_1_gt, \input );
  D_FF d_ff_24 (.D(multiplexer_5_out[8]), .C(clk), .Q(second[8]));  // open: nQ
  D_FF d_ff_25 (.D(multiplexer_5_out[7]), .C(clk), .Q(second[7]));  // open: nQ
  D_FF d_ff_26 (.D(multiplexer_5_out[6]), .C(clk), .Q(second[6]));  // open: nQ
  D_FF d_ff_27 (.D(multiplexer_5_out[5]), .C(clk), .Q(second[5]));  // open: nQ
  Multiplexer #(.Bits(16)) multiplexer_3 (.sel(and_2_out), .in_0(second), .in_1(A), .out(multiplexer_3_out));
  Multiplexer #(.Bits(16)) multiplexer_4 (
    .sel(and_3_out), .in_0(multiplexer_3_out), .in_1(Max), .out(multiplexer_4_out));
  Multiplexer #(.Bits(16)) multiplexer_5 (
    .sel(reset), .in_0(multiplexer_4_out), .in_1({16{1'b0}}), .out(multiplexer_5_out));
  D_FF d_ff_28 (.D(multiplexer_5_out[4]), .C(clk), .Q(second[4]));  // open: nQ
  D_FF d_ff_29 (.D(multiplexer_5_out[3]), .C(clk), .Q(second[3]));  // open: nQ
  D_FF d_ff_30 (.D(multiplexer_5_out[2]), .C(clk), .Q(second[2]));  // open: nQ
  D_FF d_ff_31 (.D(multiplexer_5_out[1]), .C(clk), .Q(second[1]));  // open: nQ
  D_FF d_ff_32 (.D(multiplexer_5_out[0]), .C(clk), .Q(second[0]));  // open: nQ

  // Other names for the same wires on the sheet: Max2[15:0] = second
endmodule

/* Test case Case1:
clk A input reset second
0 0 0 0 0
1 0 0 0 0
0 0 0 1 0
1 0 0 1 0
0 0  0 0 0
1 0  0 0 0
0 5 1 0 X
1 5 1 0 X
0  0 0 0 0
1  0 0 0 0
0 12 1 0 X
1 12 1 0 X
0  0 0 0 X
1  0 0 0 5
*/

/* Test case Case2:
clk A input reset second
0 0 0 0 0
1 0 0 0 0
0 0 0 1 0
1 0 0 1 0
0 0  0 0 0
1 0  0 0 0
0 5 1 0 X
1 5 1 0 X
0  0 0 0 0
1  0 0 0 0
0 15 1 0 X
1 15 1 0 X
0  0 0 0 X
1  0 0 0 5
*/

/* Test case Case3:
clk A input reset second
0 0 0 0 0
1 0 0 0 0
0 0 0 1 0
1 0 0 1 0
0 0  0 0 0
1 0  0 0 0
0 65535 1 0 X
1 65535 1 0 X
0  0 0 0 0
1  0 0 0 0
0 65524 1 0 X
1 65524 1 0 X
0  0 0 0 X
1  0 0 0 65524
*/
