// Digital circuit Prob 1 Counter.dig as structural Verilog
module Prob_1_Counter (
  input  clk,
  input  reset,
  output C,
  output B,
  output A
);

  wire and_1_out, and_2_out, and_3_out, and_4_out, and_5_out, and_6_out, DA, DB, DC, not_1_out, not_2_out,
       not_3_out, not_4_out;

  not not_1 (not_1_out, reset);
  D_FF d_ff_1 (.D(DC), .C(clk), .Q(C));  // open: nQ
  not not_2 (not_2_out, C);
  not not_3 (not_3_out, B);
  D_FF d_ff_2 (.D(DB), .C(clk), .Q(B));  // open: nQ
  not not_4 (not_4_out, A);
  and and_1 (and_1_out, not_1_out, B, not_4_out);
  and and_2 (and_2_out, not_1_out, C, A);
  and and_3 (and_3_out, not_1_out, not_2_out, A);
  and and_4 (and_4_out, not_1_out, B, not_4_out);
  and and_5 (and_5_out, not_1_out, not_2_out, not_3_out);
  and and_6 (and_6_out, not_1_out, C, B);
  D_FF d_ff_3 (.D(DA), .C(clk), .Q(A));  // open: nQ
  or or_1 (DC, and_1_out, and_2_out);
  or or_2 (DB, and_3_out, and_4_out);
  or or_3 (DA, and_5_out, and_6_out);
endmodule
