// Digital circuit Prob 2 Sqrt Temp.dig as structural Verilog
module Prob_2_Sqrt_Temp (
  input  [15:0] A,
  input  \input ,
  input  clk,
  output busy
);

  wire and_1_out, d_ff_1_nq, d_ff_2_q, d_ff_3_q, div_1_q, multiplexer_1_out, multiplexer_2_out, temp;
  wire [1:0] mul_1_mul;

  D_FF d_ff_1 (.D(\input ), .C(clk), .nQ(d_ff_1_nq));  // open: Q
  Div div_1 (.a(temp), .b(1'b0), .q(div_1_q));  // open: r
  D_FF d_ff_2 (.D(\input ), .C(clk), .Q(d_ff_2_q));  // open: nQ
  D_FF d_ff_3 (.D(d_ff_1_nq), .C(clk), .Q(d_ff_3_q));  // open: nQ
  Mul mul_1 (.a(div_1_q), .b(div_1_q), .mul(mul_1_mul));
  Multiplexer multiplexer_1 (.sel(busy), .in_0(A[0]), .in_1(temp), .out(multiplexer_1_out));
  Comparator comparator_1 (.a(A[0]), .b(mul_1_mul[0]));  // open: gt, eq, lt
  and and_1 (and_1_out, d_ff_2_q, d_ff_3_q);
  Multiplexer multiplexer_2 (.in_0(multiplexer_1_out), .out(multiplexer_2_out));  // open: sel, in_1
  T_FF t_ff_1 (.T(and_1_out), .C(clk), .Q(busy));  // open: nQ
  Register register_1 (.D(multiplexer_2_out), .C(clk), .Q(temp));  // open: en
  // Pins of 1 and 16 bits meet at A
  // Pins of 1 and 16 bits meet at 16'h2
  // Pins of 1 and 2 bits meet at mul_1_mul
endmodule
