// Digital circuit Prob 2 Sqrt V.2(Done).dig as structural Verilog
module Prob_2_Sqrt_V_2_Done (
  input  [15:0] A,
  input  \input ,
  input  clk,
  output busy,
  output [7:0] sqrt
);

  wire and_1_out, comparator_1_eq, comparator_2_lt, done, not_1_out, not_2_out;
  wire [7:0] div_2_q;
  wire [15:0] A_t, add_1_s, div_1_q, multiplexer_1_out, multiplexer_2_out, \reg ;
  wire [15:8] div_2_q_2;
  wire [31:0] mul_1_mul;

  Div #(.Bits(16)) div_1 (.a(A_t), .b(\reg ), .q(div_1_q));  // open: r
  Register #(.Bits(16)) register_1 (.D(A), .C(clk), .en(\input ), .Q(A_t));
  Add #(.Bits(16)) add_1 (.a(div_1_q), .b(\reg ), .c_i(1'b0), .s(add_1_s));  // open: c_o
  Div #(.Bits(16)) div_2 (.a(add_1_s), .b(16'h2), .q({div_2_q_2, div_2_q}));  // open: r
  not not_1 (not_1_out, done);
  Mul #(.Bits(16)) mul_1 (.a({div_2_q_2, div_2_q}), .b({div_2_q_2, div_2_q}), .mul(mul_1_mul));
  and and_1 (and_1_out, not_1_out, \input );
  Comparator #(.Bits(16)) comparator_1 (.a(A_t), .b(16'h1), .eq(comparator_1_eq));  // open: gt, lt
  D_FF d_ff_1 (.D(and_1_out), .C(clk), .Q(busy));  // open: nQ
  Multiplexer #(.Bits(16)) multiplexer_1 (.sel(busy), .in_0(A_t), .in_1(\reg ), .out(multiplexer_1_out));
  Comparator #(.Bits(32)) comparator_2 (.a({{16{1'b0}}, A_t}), .b(mul_1_mul), .lt(comparator_2_lt));  // open: gt, eq
  Multiplexer #(.Bits(16)) multiplexer_2 (
    .sel(comparator_2_lt), .in_0(multiplexer_1_out), .in_1({div_2_q_2, div_2_q}), .out(multiplexer_2_out));
  not not_2 (not_2_out, comparator_2_lt);
  Multiplexer #(.Bits(8)) multiplexer_3 (.sel(comparator_1_eq), .in_0(div_2_q), .in_1(8'h1), .out(sqrt));
  D_FF d_ff_2 (.D(not_2_out), .C(clk), .Q(done));  // open: nQ
  Register #(.Bits(16)) register_2 (.D(multiplexer_2_out), .C(clk), .en(comparator_2_lt), .Q(\reg ));
endmodule

/* Test case TestCase1:
clk A input sqrt busy
0 0 0 0 0
1 0 0 0 0
0 0 0 0 0
1 0 0 0 0
0 0 1 X X
1 0 1 X X
repeat (80) C 0 0 X X
0 0 0 0 0
1 0 0 0 0
*/

/* Test case TestCase2:
clk A input sqrt busy
0 0 0 0 0
1 0 0 0 0
0 0 0 0 0
1 0 0 0 0
0 1 1 X X
1 1 1 X X
repeat (80) C 1 0 X X
0 0 0 1 0
1 0 0 1 0
*/

/* Test case TestCase3:
clk A input sqrt busy
0 0 0 0 0
1 0 0 0 0
0 0 0 0 0
1 0 0 0 0
0 4 1 X X
1 4 1 X X
repeat (80) C 4 0 X X
0 0 0 2 0
1 0 0 2 0
*/

/* Test case TestCase4:
clk A input sqrt busy
0 0 0 0 0
1 0 0 0 0
0 0 0 0 0
1 0 0 0 0
0 9 1 X X
1 9 1 X X
repeat (80) C 9 0 X X
0 0 0 3 0
1 0 0 3 0
*/

/* Test case TestCase5:
clk A input sqrt busy
0 0 0 0 0
1 0 0 0 0
0 0 0 0 0
1 0 0 0 0
0 8 1 X X
1 8 1 X X
repeat (80) C 8 0 X X
0 0 0 2 0
1 0 0 2 0
*/
