// Digital circuit Prob 2 Sqrt.dig as structural Verilog
module Prob_2_Sqrt (
  input  [15:0] A,
  input  \input ,
  input  clk,
  output busy,
  output [7:0] sqrt
);

  wire and_1_out, comparator_1_lt, d_ff_1_q, d_ff_2_nq, d_ff_3_q, d_ff_4_q, d_ff_5_nq, d_ff_6_q, d_ff_7_q,
       done, not_1_out, or_1_out;
  wire [15:0] add_1_s, div_1_q, multiplexer_1_out, multiplexer_2_out, multiplexer_3_out, \reg ;
  wire [15:8] div_2_q;
  wire [31:0] mul_1_mul;

  Div #(.Bits(16)) div_1 (.a(multiplexer_1_out), .b(\reg ), .q(div_1_q));  // open: r
  D_FF d_ff_1 (.D(busy), .C(clk), .Q(d_ff_1_q));  // open: nQ
  Multiplexer #(.Bits(16)) multiplexer_1 (.sel(d_ff_1_q), .in_0({16{1'b0}}), .in_1(A), .out(multiplexer_1_out));
  Add #(.Bits(16)) add_1 (.a(div_1_q), .b(\reg ), .c_i(1'b0), .s(add_1_s));  // open: c_o
  D_FF d_ff_2 (.D(\input ), .C(clk), .nQ(d_ff_2_nq));  // open: Q
  Div #(.Bits(16)) div_2 (.a(add_1_s), .b(16'h2), .q({div_2_q, sqrt}));  // open: r
  Mul #(.Bits(16)) mul_1 (.a({div_2_q, sqrt}), .b({div_2_q, sqrt}), .mul(mul_1_mul));
  D_FF d_ff_3 (.D(\input ), .C(clk), .Q(d_ff_3_q));  // open: nQ
  D_FF d_ff_4 (.D(d_ff_2_nq), .C(clk), .Q(d_ff_4_q));  // open: nQ
  and and_1 (and_1_out, d_ff_3_q, d_ff_4_q);
  Multiplexer #(.Bits(16)) multiplexer_2 (.sel(busy), .in_0(multiplexer_1_out), .in_1(\reg ), .out(multiplexer_2_out));
  Comparator #(.Bits(32)) comparator_1 (
    .a({{16{1'b0}}, multiplexer_1_out}), .b(mul_1_mul), .lt(comparator_1_lt));  // open: gt, eq
  Multiplexer #(.Bits(16)) multiplexer_3 (
    .sel(comparator_1_lt), .in_0(multiplexer_2_out), .in_1({div_2_q, sqrt}), .out(multiplexer_3_out));
  not not_1 (not_1_out, comparator_1_lt);
  or or_1 (or_1_out, done, and_1_out);
  T_FF t_ff_1 (.T(or_1_out), .C(clk), .Q(busy));  // open: nQ
  D_FF d_ff_5 (.D(not_1_out), .C(clk), .nQ(d_ff_5_nq));  // open: Q
  Register #(.Bits(16)) register_1 (.D(multiplexer_3_out), .C(clk), .en(comparator_1_lt), .Q(\reg ));
  D_FF d_ff_6 (.D(not_1_out), .C(clk), .Q(d_ff_6_q));  // open: nQ
  D_FF d_ff_7 (.D(d_ff_5_nq), .C(clk), .Q(d_ff_7_q));  // open: nQ
  and and_2 (done, d_ff_6_q, d_ff_7_q);
endmodule
