// Digital circuit Prob 3 Mean.dig as structural Verilog
module Prob_3_Mean (
  input  [15:0] A,
  input  \input ,
  input  reset,
  input  clk,
  output [15:0] mean,
  output busy
);

  wire add_1_c_o, and_1_out, and_2_out, and_3_out, comparator_1_gt, d_ff_1_nq, d_ff_2_q, d_ff_3_nq,
       d_ff_5_nq, d_ff_6_q, d_ff_7_q, not_1_out, or_1_out;
  wire [15:0] A_t, add_1_s, add_2_s, counter_1_out, div_1_q, multiplexer_1_out, multiplexer_2_out;
  wire [31:0] mul_1_mul;

  D_FF d_ff_1 (.D(\input ), .C(clk), .nQ(d_ff_1_nq));  // open: Q
  and and_1 (and_1_out, \input , d_ff_1_nq);
  D_FF d_ff_2 (.D(and_1_out), .C(clk), .Q(d_ff_2_q));  // open: nQ
  not not_1 (not_1_out, clk);
  Multiplexer #(.Bits(16)) multiplexer_1 (.sel(reset), .in_0(A), .in_1({16{1'b0}}), .out(multiplexer_1_out));
  Mul #(.Bits(16)) mul_1 (.a(mean), .b(counter_1_out), .mul(mul_1_mul));
  D_FF d_ff_3 (.D(\input ), .C(not_1_out), .nQ(d_ff_3_nq));  // open: Q
  Register #(.Bits(16)) u_A (.D(multiplexer_1_out), .C(not_1_out), .en(d_ff_2_q), .Q(A_t));
  and and_2 (and_2_out, \input , d_ff_3_nq);
  Add #(.Bits(16)) add_1 (.a(mul_1_mul[15:0]), .b(A_t), .c_i(1'b0), .s(add_1_s), .c_o(add_1_c_o));
  Counter #(.Bits(16)) counter_1 (.en(busy), .C(clk), .clr(reset), .out(counter_1_out));  // open: ovf
  D_FF d_ff_4 (.D(and_2_out), .C(not_1_out), .Q(busy));  // open: nQ
  Add #(.Bits(16)) add_2 (.a(add_1_s), .b({16{1'b0}}), .c_i(add_1_c_o), .s(add_2_s));  // open: c_o
  Div #(.Bits(16)) div_1 (.a(add_2_s), .b(counter_1_out), .q(div_1_q));  // open: r
  Multiplexer #(.Bits(16)) multiplexer_2 (.sel(reset), .in_0(div_1_q), .in_1({16{1'b0}}), .out(multiplexer_2_out));
  Comparator #(.Bits(16)) comparator_1 (.a(div_1_q), .b(mean), .gt(comparator_1_gt));  // open: eq, lt
  Register #(.Bits(16)) u_Mean (.D(multiplexer_2_out), .C(not_1_out), .en(or_1_out), .Q(mean));
  D_FF d_ff_5 (.D(comparator_1_gt), .C(clk), .nQ(d_ff_5_nq));  // open: Q
  D_FF d_ff_6 (.D(d_ff_5_nq), .C(clk), .Q(d_ff_6_q));  // open: nQ
  D_FF d_ff_7 (.D(comparator_1_gt), .C(clk), .Q(d_ff_7_q));  // open: nQ
  and and_3 (and_3_out, d_ff_6_q, d_ff_7_q);
  or or_1 (or_1_out, and_3_out, reset);

  // Other names for the same wires on the sheet: start = busy
endmodule

/* Test case Case1:
clk A input reset mean busy
0 0 0 0 0 0
1 0 0 0 0 0
0 0 0 1 0 0
1 0 0 1 0 0
0 0 0 0 0 0
1 0 0 0 0 0
0 5 1 0 X X
1 5 1 0 X X
0 5 0 0 X X
1 5 0 0 X X
loop(x,500)
end loop
0 0 0 0 5 0
1 0 0 0 5 0
*/

/* Test case Case2:
clk A input reset mean busy
0 0 0 0 0 0
1 0 0 0 0 0
0 0 0 1 0 0
1 0 0 1 0 0
0 0 0 0 0 0
1 0 0 0 0 0
0 5 1 0 X X
1 5 1 0 X X
0 5 0 0 X X
1 5 0 0 X X
loop(x,500)
end loop
0 0 0 0 5 0
1 0 0 0 5 0
0 15 1 0 X X
1 15 1 0 X X
0 15 0 0 X X
1 15 0 0 X X
loop(x,500)
end loop
0 0 0 0 10 0
1 0 0 0 10 0
*/

/* Test case Case3:
clk A input reset mean busy
0 0 0 0 0 0
1 0 0 0 0 0
0 0 0 1 0 0
1 0 0 1 0 0
0 0 0 0 0 0
1 0 0 0 0 0
0 65535 1 0 X X
1 65535 1 0 X X
0 65535 0 0 X X
1 65535 0 0 X X
loop(x,500)
end loop
0 0 0 0 65535 0
1 0 0 0 65535 0
0 65535 1 0 X X
1 65535 1 0 X X
0 65535 0 0 X X
1 65535 0 0 X X
loop(x,500)
end loop
0 0 0 0 65535 0
1 0 0 0 65535 0
*/

/* Test case Case4:
clk A input reset mean busy
0 0 0 0 0 0
1 0 0 0 0 0
0 0 0 1 0 0
1 0 0 1 0 0
0 0 0 0 0 0
1 0 0 0 0 0
0 1 1 0 X X
1 1 1 0 X X
0 1 0 0 X X
1 1 0 0 X X
loop(x,500)
end loop
0 0 0 0 1 0
1 0 0 0 1 0
0 2 1 0 X X
1 2 1 0 X X
0 2 0 0 X X
1 2 0 0 X X
loop(x,500)
end loop
0 0 0 0 1 0
1 0 0 0 1 0
0 3 1 0 X X
1 3 1 0 X X
0 3 0 0 X X
1 3 0 0 X X
loop(x,500)
end loop
0 0 0 0 2 0
1 0 0 0 2 0
0 4 1 0 X X
1 4 1 0 X X
0 4 0 0 X X
1 4 0 0 X X
loop(x,500)
end loop
0 0 0 0 2 0
1 0 0 0 2 0
0 5 1 0 X X
1 5 1 0 X X
0 5 0 0 X X
1 5 0 0 X X
loop(x,500)
end loop
0 0 0 0 3 0
1 0 0 0 3 0
0 6 1 0 X X
1 6 1 0 X X
0 6 0 0 X X
1 6 0 0 X X
loop(x,500)
end loop
0 0 0 0 3 0
1 0 0 0 3 0
0 7 1 0 X X
1 7 1 0 X X
0 7 0 0 X X
1 7 0 0 X X
loop(x,500)
end loop
0 0 0 0 4 0
1 0 0 0 4 0
0 8 1 0 X X
1 8 1 0 X X
0 8 0 0 X X
1 8 0 0 X X
loop(x,500)
end loop
0 0 0 0 4 0
1 0 0 0 4 0
0 9 1 0 X X
1 9 1 0 X X
0 9 0 0 X X
1 9 0 0 X X
loop(x,500)
end loop
0 0 0 0 5 0
1 0 0 0 5 0
0 10 1 0 X X
1 10 1 0 X X
0 10 0 0 X X
1 10 0 0 X X
loop(x,500)
end loop
0 0 0 0 5 0
1 0 0 0 5 0
0 11 1 0 X X
1 11 1 0 X X
0 11 0 0 X X
1 11 0 0 X X
loop(x,500)
end loop
0 0 0 0 6 0
1 0 0 0 6 0
0 12 1 0 X X
1 12 1 0 X X
0 12 0 0 X X
1 12 0 0 X X
loop(x,500)
end loop
0 0 0 0 6 0
1 0 0 0 6 0
0 13 1 0 X X
1 13 1 0 X X
0 13 0 0 X X
1 13 0 0 X X
loop(x,500)
end loop
0 0 0 0 7 0
1 0 0 0 7 0
0 14 1 0 X X
1 14 1 0 X X
0 14 0 0 X X
1 14 0 0 X X
loop(x,500)
end loop
0 0 0 0 7 0
1 0 0 0 7 0
0 15 1 0 X X
1 15 1 0 X X
0 15 0 0 X X
1 15 0 0 X X
loop(x,500)
end loop
0 0 0 0 8 0
1 0 0 0 8 0
*/

/* Test case Case5:
clk A input reset mean busy
0 0 0 0 0 0
1 0 0 0 0 0
0 0 0 1 0 0
1 0 0 1 0 0
0 0 0 0 0 0
1 0 0 0 0 0
0 0 1 0 X X
1 0 1 0 X X
0 0 0 0 X X
1 0 0 0 X X
loop(x,500)
end loop
0 0 0 0 0 0
1 0 0 0 0 0
0 0 1 0 X X
1 0 1 0 X X
0 0 0 0 X X
1 0 0 0 X X
loop(x,500)
end loop
0 0 0 0 0 0
1 0 0 0 0 0
0 0 1 0 X X
1 0 1 0 X X
0 0 0 0 X X
1 0 0 0 X X
loop(x,500)
end loop
0 0 0 0 0 0
1 0 0 0 0 0
0 0 1 0 X X
1 0 1 0 X X
0 0 0 0 X X
1 0 0 0 X X
loop(x,500)
end loop
0 0 0 0 0 0
1 0 0 0 0 0
0 0 1 0 X X
1 0 1 0 X X
0 0 0 0 X X
1 0 0 0 X X
loop(x,500)
end loop
0 0 0 0 0 0
1 0 0 0 0 0
0 0 1 0 X X
1 0 1 0 X X
0 0 0 0 X X
1 0 0 0 X X
loop(x,500)
end loop
0 0 0 0 0 0
1 0 0 0 0 0
0 0 1 0 X X
1 0 1 0 X X
0 0 0 0 X X
1 0 0 0 X X
loop(x,500)
end loop
0 0 0 0 0 0
1 0 0 0 0 0
0 0 1 0 X X
1 0 1 0 X X
0 0 0 0 X X
1 0 0 0 X X
loop(x,500)
end loop
0 0 0 0 0 0
1 0 0 0 0 0
0 0 1 0 X X
1 0 1 0 X X
0 0 0 0 X X
1 0 0 0 X X
loop(x,500)
end loop
0 0 0 0 0 0
1 0 0 0 0 0
0 0 1 0 X X
1 0 1 0 X X
0 0 0 0 X X
1 0 0 0 X X
loop(x,500)
end loop
0 0 0 0 0 0
1 0 0 0 0 0
*/
