// Digital circuit 01_Raw.dig as structural Verilog
module _01_Raw (
  input  [3:0] In,
  output A,
  output B,
  output C,
  output D,
  output E,
  output F,
  output G
);

  wire and_1_out, and_2_out, and_3_out, and_4_out, and_5_out, and_6_out, and_7_out, and_8_out, and_9_out;

  and and_1 (and_1_out, ~In[0], ~In[1], ~In[2], ~In[3]);  // And
  and and_2 (and_2_out, In[0], ~In[1], ~In[2], ~In[3]);  // And
  and and_3 (and_3_out, ~In[0], In[1], ~In[2], ~In[3]);  // And
  and and_4 (and_4_out, In[0], In[1], ~In[2], ~In[3]);  // And
  and and_5 (and_5_out, ~In[0], ~In[1], In[2], ~In[3]);  // And
  and and_6 (and_6_out, In[0], ~In[1], In[2], ~In[3]);  // And
  and and_7 (and_7_out, ~In[0], In[1], In[2], ~In[3]);  // And
  and and_8 (and_8_out, In[0], In[1], In[2], ~In[3]);  // And
  and and_9 (and_9_out, ~In[0], ~In[1], ~In[2], In[3]);  // And
  and and_10 (A, ~and_2_out, ~and_5_out);  // And
  and and_11 (B, ~and_6_out, ~and_7_out);  // And
  and and_12 (D, ~and_2_out, ~and_5_out, ~and_8_out);  // And
  or or_1 (E, and_1_out, and_3_out, and_7_out, and_9_out);
  and and_13 (F, ~and_2_out, ~and_3_out, ~and_4_out);  // And
  and and_14 (G, ~and_1_out, ~and_2_out, ~and_8_out);  // And
  not not_1 (C, and_3_out);
  Seven_Seg seven_seg_1 (.a(A), .b(B), .c(C), .d(D), .e(E), .f(F), .g(G), .dp(1'b0));
endmodule
