// Digital circuit 03-01_with_Screen.dig as structural Verilog
module _03_01_with_Screen (
  input  [3:0] In,
  output A,
  output B,
  output C,
  output D,
  output E,
  output F,
  output G
);

  wire and_1_out, and_2_out, and_3_out, and_4_out, and_5_out, and_6_out, and_7_out, and_8_out;

  and and_1 (and_1_out, ~In[0], ~In[2]);  // And
  and and_2 (and_2_out, ~In[0], In[1]);  // And
  and and_3 (and_3_out, In[0], In[1]);
  and and_4 (and_4_out, In[0], ~In[1], In[2]);  // And
  and and_5 (and_5_out, In[0], ~In[2]);  // And
  and and_6 (and_6_out, In[1], ~In[2]);  // And
  and and_7 (and_7_out, ~In[0], ~In[1]);  // And
  and and_8 (and_8_out, ~In[0], In[2]);  // And
  or or_1 (A, and_1_out, and_2_out, and_3_out, and_4_out, In[3]);
  or or_2 (B, and_5_out, and_6_out, and_3_out, and_7_out);
  or or_3 (C, and_5_out, and_8_out, and_3_out, and_7_out, and_4_out);
  or or_4 (D, and_1_out, and_2_out, and_6_out, and_4_out, In[3]);
  or or_5 (E, and_1_out, and_2_out);
  or or_6 (F, and_8_out, and_7_out, and_4_out, In[3]);
  or or_7 (G, and_6_out, and_8_out, and_4_out, In[3]);
  Seven_Seg seven_seg_1 (.a(A), .b(B), .c(C), .d(D), .e(E), .f(F), .g(G), .dp(1'b0));
endmodule
