// Digital circuit 03-02.dig as structural Verilog
module _03_02 (
  input  [2:0] In,
  output [7:0] Z
);

  wire and_1_out, and_2_out;
  wire [6:6] and_3_out, and_4_out, and_5_out, and_6_out, and_7_out, and_8_out, or_1_out;

  and and_1 (and_1_out, In[0], In[1], ~In[2]);  // And
  and and_2 (and_2_out, In[0], ~In[1], In[2]);  // And
  and and_3 (and_3_out[6], ~In[0], ~In[1], In[2]);  // And
  and and_4 (and_4_out[6], ~In[0], In[1], In[2]);  // And
  and and_5 (and_5_out[6], In[0], In[1], In[2]);
  and and_6 (and_6_out[6], ~In[0], ~In[1], ~In[2]);  // And
  and and_7 (and_7_out[6], In[0], ~In[1], ~In[2]);  // And
  and and_8 (and_8_out[6], ~In[0], In[1], ~In[2]);  // And
  or or_1 (or_1_out[6], and_1_out, and_2_out);
  assign Z = {1'b0, and_6_out[6], 3'b000, and_6_out[6], 2'b00} | {1'b0, {2{and_7_out[6]}}, 1'b0, and_7_out[6], 2'b00, and_7_out[6]} | {1'b0, {2{and_8_out[6]}}, 2'b00, {3{and_8_out[6]}}} | {1'b0, or_1_out[6], 2'b00, {2{or_1_out[6]}}, 2'b00} | {1'b0, {2{and_4_out[6]}}, 4'b0000, and_4_out[6]} | {1'b0, {2{and_5_out[6]}}, 3'b000, and_5_out[6], 1'b0} | {1'b0, {2{and_3_out[6]}}, 1'b0, {4{and_3_out[6]}}} | {1'b0, or_1_out[6], 2'b00, {2{or_1_out[6]}}, 2'b00};  // Or or_2, 8 bits wide
endmodule
