// Digital circuit 03-03.dig as structural Verilog
module _03_03 (
  input  [3:0] In,
  input  [1:0] Selector,
  output [3:0] Output
);

  wire and_1_out, and_3_out, and_4_out, and_5_out, and_6_out, and_7_out, and_8_out, and_9_out, and_10_out,
       and_11_out, and_12_out, and_13_out, and_14_out, and_15_out, and_16_out, and_17_out, and_18_out,
       and_19_out, and_20_out, and_21_out, and_22_out, and_23_out, S1_I2__I1_I0;

  and and_1 (and_1_out, Selector[0], Selector[1], In[0], In[1]);
  and and_2 (S1_I2__I1_I0, Selector[1], In[2], ~In[1], In[0]);  // And
  and and_3 (and_3_out, ~Selector[0], In[2], In[0]);  // And
  and and_4 (and_4_out, ~Selector[0], In[2], In[1]);  // And
  and and_5 (and_5_out, Selector[1], Selector[0], ~In[2], ~In[1], In[0]);  // And
  and and_6 (and_6_out, ~Selector[1], ~Selector[0], ~In[2], In[0]);  // And
  and and_7 (and_7_out, ~Selector[1], ~Selector[0], ~In[2], In[1]);  // And
  and and_8 (and_8_out, ~Selector[1], Selector[0], In[2], ~In[1]);  // And
  and and_9 (and_9_out, In[2], ~In[1], ~In[0]);  // And
  and and_10 (and_10_out, ~Selector[1], Selector[0], In[3]);  // And
  and and_11 (and_11_out, Selector[1], ~Selector[0], In[3]);  // And
  and and_12 (and_12_out, Selector[0], In[1], In[2]);
  and and_13 (and_13_out, Selector[1], In[2], In[1]);
  and and_14 (and_14_out, ~Selector[1], ~Selector[0], ~In[1], ~In[0]);  // And
  and and_15 (and_15_out, Selector[1], Selector[0], In[1], ~In[0]);  // And
  and and_16 (and_16_out, ~Selector[1], Selector[0], ~In[2], In[1]);  // And
  and and_17 (and_17_out, Selector[1], ~Selector[0], ~In[2], In[1]);  // And
  and and_18 (and_18_out, ~Selector[1], ~Selector[0], In[1], In[0]);  // And
  and and_19 (and_19_out, ~Selector[1], Selector[0], In[2], ~In[1]);  // And
  and and_20 (and_20_out, Selector[1], In[3]);
  and and_21 (and_21_out, ~Selector[1], In[1], ~In[0]);  // And
  and and_22 (and_22_out, Selector[0], ~In[1], In[0]);  // And
  and and_23 (and_23_out, Selector[1], In[0]);
  or or_1 (Output[3], and_1_out, S1_I2__I1_I0, and_3_out, and_4_out, In[3]);
  or or_2 (Output[2], and_5_out, and_6_out, and_7_out, and_8_out, and_9_out, and_10_out, and_11_out, and_12_out, and_13_out);
  or or_3 (Output[1], S1_I2__I1_I0, and_14_out, and_15_out, and_16_out, and_17_out, and_18_out, and_19_out, and_20_out);
  or or_4 (Output[0], and_14_out, and_21_out, and_22_out, and_23_out);
endmodule
