// Digital circuit 03-04.dig as structural Verilog
module _03_04 (
  input  [6:0] In,
  output [6:0] Output
);

  wire _3_to_8_decoder_1_y1, _3_to_8_decoder_1_y2, _3_to_8_decoder_1_y3, _3_to_8_decoder_1_y4,
       _3_to_8_decoder_1_y5, _3_to_8_decoder_1_y6, _3_to_8_decoder_1_y7, _3_to_8_decoder_1_y8, xor_1_out,
       xor_2_out, xor_3_out;

  xor xor_1 (xor_1_out, In[3], In[2], In[1], In[0]);
  xor xor_2 (xor_2_out, In[5], In[4], In[1], In[0]);
  xor xor_3 (xor_3_out, In[6], In[4], In[2], In[0]);
  _3_to_8_Decoder _3_to_8_decoder_1 (
    .C1(xor_1_out), .C2(xor_2_out), .C3(xor_3_out), .Y1(_3_to_8_decoder_1_y1), .Y2(_3_to_8_decoder_1_y2),
    .Y3(_3_to_8_decoder_1_y3), .Y4(_3_to_8_decoder_1_y4), .Y5(_3_to_8_decoder_1_y5),
    .Y6(_3_to_8_decoder_1_y6), .Y7(_3_to_8_decoder_1_y7), .Y8(_3_to_8_decoder_1_y8));
  xor xor_4 (Output[0], In[0], _3_to_8_decoder_1_y8);
  xor xor_5 (Output[1], In[1], _3_to_8_decoder_1_y7);
  xor xor_6 (Output[2], In[2], _3_to_8_decoder_1_y6);
  xor xor_7 (Output[3], In[3], _3_to_8_decoder_1_y5);
  xor xor_8 (Output[4], In[4], _3_to_8_decoder_1_y4);
  xor xor_9 (Output[5], In[5], _3_to_8_decoder_1_y3);
  xor xor_10 (Output[6], In[6], _3_to_8_decoder_1_y2);
endmodule
