// Digital circuit 03-04_grader.dig as structural Verilog
module _03_04_grader (
  input  [6:0] In,
  output [6:0] Output
);

  wire and_1_out, and_2_out, and_3_out, and_4_out, and_5_out, and_6_out, and_7_out, and_8_out, xor_1_out,
       xor_2_out, xor_3_out;

  xor xor_1 (xor_1_out, In[3], In[2], In[1], In[0]);
  xor xor_2 (xor_2_out, In[5], In[4], In[1], In[0]);
  xor xor_3 (xor_3_out, In[6], In[4], In[2], In[0]);
  and and_1 (and_1_out, ~xor_1_out, ~xor_2_out, ~xor_3_out);  // And
  and and_2 (and_2_out, ~xor_1_out, ~xor_2_out, xor_3_out);  // And
  and and_3 (and_3_out, ~xor_1_out, xor_2_out, ~xor_3_out);  // And
  and and_4 (and_4_out, ~xor_1_out, xor_2_out, xor_3_out);  // And
  and and_5 (and_5_out, xor_1_out, ~xor_2_out, ~xor_3_out);  // And
  and and_6 (and_6_out, xor_1_out, ~xor_2_out, xor_3_out);  // And
  and and_7 (and_7_out, xor_1_out, xor_2_out, ~xor_3_out);  // And
  and and_8 (and_8_out, xor_1_out, xor_2_out, xor_3_out);
  xor xor_4 (Output[0], In[0], and_8_out);
  xor xor_5 (Output[1], In[1], and_7_out);
  xor xor_6 (Output[2], In[2], and_6_out);
  xor xor_7 (Output[3], In[3], and_5_out);
  xor xor_8 (Output[4], In[4], and_4_out);
  xor xor_9 (Output[5], In[5], and_3_out);
  xor xor_10 (Output[6], In[6], and_2_out);
endmodule
