// Digital circuit 3_to_8_Decoder.dig as structural Verilog
module _3_to_8_Decoder (
  input  C1,
  input  C2,
  input  C3,
  output Y1,
  output Y2,
  output Y3,
  output Y4,
  output Y5,
  output Y6,
  output Y7,
  output Y8
);

  and and_1 (Y1, ~C3, ~C2, ~C1);  // And
  and and_2 (Y2, ~C3, ~C2, C1);  // And
  and and_3 (Y3, ~C3, C2, ~C1);  // And
  and and_4 (Y4, ~C3, C2, C1);  // And
  and and_5 (Y5, C3, ~C2, ~C1);  // And
  and and_6 (Y6, C3, ~C2, C1);  // And
  and and_7 (Y7, C3, C2, ~C1);  // And
  and and_8 (Y8, C3, C2, C1);
endmodule
