// Digital circuit Fulladder_NAND.dig as structural Verilog
module Fulladder_NAND (
  input  A,
  input  B,
  input  C,
  output Sum,
  output Cout
);

  wire nand_1_out, nand_2_out, nand_3_out, nand_4_out, nand_5_out, nand_6_out, nand_7_out;

  nand nand_1 (nand_1_out, A, B);
  nand nand_2 (nand_2_out, A, nand_1_out);
  nand nand_3 (nand_3_out, nand_1_out, B);
  nand nand_4 (nand_4_out, nand_2_out, nand_3_out);
  nand nand_5 (nand_5_out, nand_4_out, C);
  nand nand_6 (nand_6_out, nand_4_out, nand_5_out);
  nand nand_7 (nand_7_out, nand_5_out, C);
  nand nand_8 (Sum, nand_6_out, nand_7_out);
  nand nand_9 (Cout, nand_5_out, nand_1_out);
endmodule
