// Digital circuit M1.dig as structural Verilog
module M1 (
  input  [3:0] A,
  input  [3:0] B,
  input  [2:0] S,
  input  C,
  output [3:0] out
);

  wire [3:0] add_1_s, add_2_s, add_3_s, add_4_s, add_5_s, add_6_s, barrelshifter_1_out, barrelshifter_2_out,
       neg_1_out, not_1_out;

  assign not_1_out = ~B;  // Not not_1, 4 bits wide
  BarrelShifter #(.Bits(4), .barrelShifterMode("arithmetic")) barrelshifter_1 (
    .in(A), .shift(3'b001), .out(barrelshifter_1_out));
  BarrelShifter #(.Bits(4), .barrelShifterMode("arithmetic"), .direction("right")) barrelshifter_2 (
    .in(A), .shift(3'b001), .out(barrelshifter_2_out));
  Add #(.Bits(4)) add_1 (.a(A), .b(4'b0000), .c_i(C), .s(add_1_s));  // open: c_o
  Add #(.Bits(4)) add_2 (.a(A), .b(4'b1111), .c_i(C), .s(add_2_s));  // open: c_o
  Add #(.Bits(4)) add_3 (.a(A), .b(B), .c_i(C), .s(add_3_s));  // open: c_o
  Add #(.Bits(4)) add_4 (.a(A), .b(not_1_out), .c_i(C), .s(add_4_s));  // open: c_o
  Neg #(.Bits(4)) neg_1 (.in(A), .out(neg_1_out));
  Add #(.Bits(4)) add_5 (.a(4'b0000), .b(B), .c_i(C), .s(add_5_s));  // open: c_o
  Add #(.Bits(4)) add_6 (.a(neg_1_out), .b(4'b1111), .c_i(C), .s(add_6_s));  // open: c_o
  Multiplexer #(.Selector_Bits(3), .Bits(4)) multiplexer_1 (
    .sel(S), .in_0(add_1_s), .in_1(add_2_s), .in_2(add_3_s), .in_3(add_4_s), .in_4(add_6_s), .in_5(add_5_s),
    .in_6(barrelshifter_1_out), .in_7(barrelshifter_2_out), .out(out));
endmodule
