// Digital circuit 03.dig as structural Verilog
module _03 (
  input  K,
  input  J,
  input  Clear,
  input  Clock,
  output Q,
  output Q_2
);

  wire and_1_out, and_2_out, and_3_out, and_4_out, nor_1_out, nor_2_out, not_1_out, or_1_out;

  and and_1 (and_1_out, Q_2, K, Clock);
  and and_2 (and_2_out, Q, J, Clock);
  nor nor_1 (nor_1_out, and_1_out, Clear, nor_2_out);
  nor nor_2 (nor_2_out, nor_1_out, and_2_out);
  not not_1 (not_1_out, Clock);
  or or_1 (or_1_out, Clear, not_1_out);
  and and_3 (and_3_out, or_1_out, nor_1_out);
  and and_4 (and_4_out, nor_2_out, or_1_out);
  nor nor_3 (Q, and_3_out, Q_2);
  nor nor_4 (Q_2, Q, and_4_out);
endmodule

/* Test case test 1:
K J \Clear Clock Q \Q
0 0 1 0 0 1
0 0 1 1 0 1
0 1 0 0 0 1
0 1 0 1 0 1
0 1 0 0 1 0
1 0 0 1 1 0
1 0 0 0 0 1
0 0 0 1 0 1
0 0 0 0 0 1
0 1 0 1 0 1
0 1 0 0 1 0
*/
