// Digital circuit 04.dig as structural Verilog
module _04 (
  input  D,
  input  Clear,
  input  Clock,
  output Q,
  output Q_2
);

  wire nand_1_out, nand_2_out, nor_1_out, nor_2_out, nor_3_out, nor_4_out, nor_5_out, nor_6_out, not_1_out,
       not_2_out, not_3_out, not_4_out;

  nand nand_1 (nand_1_out, Clear, nand_2_out);
  nand nand_2 (nand_2_out, nand_1_out, Clock);
  nor nor_1 (nor_1_out, ~not_4_out, ~not_2_out);  // NOr
  nor nor_2 (nor_2_out, ~not_1_out, ~Clock);  // NOr
  nor nor_3 (nor_3_out, ~not_2_out, ~Clock, ~not_4_out);  // NOr
  nor nor_4 (nor_4_out, ~not_3_out, ~nand_1_out, ~D);  // NOr
  not not_1 (not_1_out, nor_1_out);
  not not_2 (not_2_out, nor_2_out);
  not not_3 (not_3_out, nor_3_out);
  not not_4 (not_4_out, nor_4_out);
  nor nor_5 (nor_5_out, ~not_2_out, ~Q_2);  // NOr
  nor nor_6 (nor_6_out, ~Q, ~not_3_out);  // NOr
  not not_5 (Q, nor_5_out);
  not not_6 (Q_2, nor_6_out);
endmodule
