// Digital circuit Template.dig as structural Verilog
module Template (
  input  Clear,
  input  Clock,
  input  T,
  output Q,
  output Q_2
);

  wire and_1_out, and_2_out, nand_1_out, nand_2_out, nand_3_out, nand_4_out;

  nand nand_1 (nand_1_out, nand_4_out, nand_2_out);
  nand nand_2 (nand_2_out, nand_1_out, Clock);
  nand nand_3 (nand_3_out, nand_2_out, Clock, nand_4_out);
  nand nand_4 (nand_4_out, nand_3_out, T, Clear);
  and and_1 (and_1_out, Q, nand_4_out);
  and and_2 (and_2_out, nand_4_out, Q_2);
  nor nor_1 (Q, and_1_out, Q_2);
  nor nor_2 (Q_2, Q, and_2_out);
endmodule
