// Digital circuit 01.dig as structural Verilog
module _01 (
  input  A,
  input  B,
  input  C,
  input  D,
  input  P,
  input  T,
  input  Clr,
  input  Load,
  input  Clk,
  output QA,
  output QB,
  output QC,
  output QD,
  output RCO,
  output QA_2,
  output QB_2,
  output QC_2,
  output QD_2
);

  wire and_1_out, and_2_out, and_3_out, and_4_out, and_5_out, and_6_out, and_7_out, and_8_out, and_9_out,
       and_10_out, and_11_out, and_12_out, and_13_out, and_14_out, not_1_out, or_1_out, or_2_out, or_3_out,
       or_4_out;
  wire [3:0] add_1_s;

  and and_1 (and_1_out, Clr, Load, P, T);
  Add #(.Bits(4)) add_1 (.a({QD, QC, QB, QA}), .b(4'b0001), .c_i(1'b0), .s(add_1_s));  // open: c_o
  not not_1 (not_1_out, Clr);
  and and_2 (and_2_out, and_1_out, add_1_s[0]);
  and and_3 (and_3_out, and_1_out, add_1_s[1]);
  and and_4 (and_4_out, and_1_out, add_1_s[2]);
  and and_5 (and_5_out, and_1_out, add_1_s[3]);
  _74163 _74163_1 (
    .pin1(not_1_out), .pin2(Clk), .pin3(A), .pin4(B), .pin5(C), .pin6(D), .pin7(Load), .pin8(1'b0), .pin9(P),
    .pin10(T), .pin11(QD_2), .pin12(QC_2), .pin13(QB_2), .pin14(QA_2), .pin16(1'b1));  // open: pin15
  and and_6 (and_6_out, A, ~Load);  // And
  or or_1 (or_1_out, and_6_out, and_2_out);
  and and_7 (and_7_out, B, ~Load);  // And
  and and_8 (and_8_out, C, ~Load);  // And
  and and_9 (and_9_out, D, ~Load);  // And
  or or_2 (or_2_out, and_7_out, and_3_out);
  or or_3 (or_3_out, and_8_out, and_4_out);
  or or_4 (or_4_out, and_9_out, and_5_out);
  and and_10 (and_10_out, ~Clr, Load);  // And
  and and_11 (and_11_out, or_1_out, ~and_10_out);  // And
  and and_12 (and_12_out, or_2_out, ~and_10_out);  // And
  and and_13 (and_13_out, or_3_out, ~and_10_out);  // And
  and and_14 (and_14_out, or_4_out, ~and_10_out);  // And
  D_FF d_ff_1 (.D(and_11_out), .C(Clk), .Q(QA));  // open: nQ
  D_FF d_ff_2 (.D(and_12_out), .C(Clk), .Q(QB));  // open: nQ
  D_FF d_ff_3 (.D(and_13_out), .C(Clk), .Q(QC));  // open: nQ
  D_FF d_ff_4 (.D(and_14_out), .C(Clk), .Q(QD));  // open: nQ
  and and_15 (RCO, QA, QB, QC, QD);
endmodule
