// Digital circuit 04.dig as structural Verilog
module _04 (
  input  P,
  input  clock,
  input  Clr,
  output Z
);

  wire and_1_out, and_2_out, D0_q, D1_q, D3_q, multiplexer_1_out, multiplexer_2_out;

  D_FF D3 (.D(P), .C(clock), .Q(D3_q));  // open: nQ
  Multiplexer multiplexer_1 (.sel(Clr), .in_0(D3_q), .in_1(1'b0), .out(multiplexer_1_out));
  and and_1 (and_1_out, D0_q, multiplexer_1_out);
  and and_2 (and_2_out, ~D1_q, ~D0_q, multiplexer_1_out);  // And
  D_FF D1 (.D(and_1_out), .C(clock), .Q(D1_q));  // open: nQ
  D_FF D0 (.D(and_2_out), .C(clock), .Q(D0_q));  // open: nQ
  Multiplexer multiplexer_2 (.sel(Clr), .in_0(and_2_out), .in_1(1'b0), .out(multiplexer_2_out));
  D_FF D2 (.D(multiplexer_2_out), .C(clock), .Q(Z));  // open: nQ
endmodule
