// Digital circuit 05.dig as structural Verilog
module _05 (
  input  P,
  input  clock,
  input  Clr,
  output Z
);

  wire and_1_out, multiplexer_1_out, Next_State_q, xor_1_out;

  and and_1 (and_1_out, P, ~Clr);  // And
  D_FF Next_State (.D(and_1_out), .C(clock), .Q(Next_State_q));  // open: nQ
  xor xor_1 (xor_1_out, Next_State_q, and_1_out);
  Multiplexer multiplexer_1 (.sel(P), .in_0(1'b0), .in_1(xor_1_out), .out(multiplexer_1_out));
  D_FF Current_State (.D(multiplexer_1_out), .C(clock), .Q(Z));  // open: nQ
endmodule
