// Digital circuit Vending.dig as structural Verilog
module Vending (
  input  reset,
  input  P5,
  input  P10,
  input  P20,
  input  Pcoffee,
  input  Ptea,
  input  Pchange,
  input  Pnext,
  input  clock,
  output [5:0] Balance,
  output CoffeeOut,
  output TeaOut,
  output [1:0] Change5,
  output [1:0] Change10,
  output [1:0] Change20
);

  wire Add5, Add10, Add20, and_1_out, and_2_out, and_3_out, and_7_out, and_8_out, BuyCoffee, BuyTea,
       Coffee_gt, d_ff_1_nq, d_ff_2_nq, d_ff_3_nq, d_ff_5_q, d_ff_6_q, d_ff_7_q, d_ff_8_q, d_ff_9_q,
       d_ff_10_q, d_ff_14_nq, d_ff_15_nq, d_ff_16_q, d_ff_17_q, d_ff_18_q, d_ff_19_q, d_ff_20_q, d_ff_21_q,
       d_ff_22_nq, d_ff_23_nq, d_ff_24_q, d_ff_25_q, d_ff_26_q, d_ff_27_q, MoneyChange, NextDrink, or_1_out,
       or_2_out, or_3_out, P5_lt, P10_lt, P20_lt, rs_ff_as_1_q, rs_ff_as_2_q, Tea_gt;
  wire [5:0] Add_Balance_s, Buy_Drink_s, C5_q, C10_q, C10_r, C20_q, C20_r, d_ff_4_q, multiplexer_1_out,
       multiplexer_2_out, multiplexer_3_out, multiplexer_5_out, multiplexer_6_out, multiplexer_7_out;
  wire [5:2] d_ff_11_q, d_ff_12_q, d_ff_13_q;

  Comparator #(.Bits(6)) u_P5 (.a(Balance), .b(6'b101110), .lt(P5_lt));  // open: gt, eq
  Comparator #(.Bits(6)) u_P10 (.a(Balance), .b(6'b101001), .lt(P10_lt));  // open: gt, eq
  Comparator #(.Bits(6)) u_P20 (.a(Balance), .b(6'b011111), .lt(P20_lt));  // open: gt, eq
  Multiplexer #(.Selector_Bits(3), .Bits(6)) multiplexer_1 (
    .sel({Add20, Add10, Add5}), .in_0({6{1'b0}}), .in_1(6'b000101), .in_2(6'b001010), .in_3({6{1'b0}}),
    .in_4(6'b010100), .in_5({6{1'b0}}), .in_6({6{1'b0}}), .in_7({6{1'b0}}), .out(multiplexer_1_out));
  Multiplexer #(.Selector_Bits(2), .Bits(6)) multiplexer_2 (
    .sel({BuyCoffee, BuyTea}), .in_0({6{1'b0}}), .in_1(6'b010100), .in_2(6'b011001), .in_3({6{1'b0}}),
    .out(multiplexer_2_out));
  Add #(.Bits(6)) Add_Balance (.a(Balance), .b(multiplexer_1_out), .c_i(1'b0), .s(Add_Balance_s));  // open: c_o
  Sub #(.Bits(6)) Buy_Drink (.a(Balance), .b(multiplexer_2_out), .c_i(1'b0), .s(Buy_Drink_s));  // open: c_o
  or or_1 (or_1_out, BuyTea, BuyCoffee);
  and and_1 (and_1_out, P5_lt, P5, ~CoffeeOut, ~TeaOut);  // And
  and and_2 (and_2_out, P10_lt, P10, ~CoffeeOut, ~TeaOut);  // And
  and and_3 (and_3_out, P20_lt, P20, ~CoffeeOut, ~TeaOut);  // And
  Multiplexer #(.Bits(6)) multiplexer_3 (
    .sel(or_1_out), .in_0(Add_Balance_s), .in_1(Buy_Drink_s), .out(multiplexer_3_out));
  D_FF d_ff_1 (.D(and_1_out), .C(clock), .nQ(d_ff_1_nq));  // open: Q
  D_FF d_ff_2 (.D(and_2_out), .C(clock), .nQ(d_ff_2_nq));  // open: Q
  D_FF d_ff_3 (.D(and_3_out), .C(clock), .nQ(d_ff_3_nq));  // open: Q
  D_FF #(.Bits(6)) d_ff_4 (.D(multiplexer_3_out), .C(clock), .Q(d_ff_4_q));  // open: nQ
  D_FF d_ff_5 (.D(and_1_out), .C(clock), .Q(d_ff_5_q));  // open: nQ
  D_FF d_ff_6 (.D(d_ff_1_nq), .C(clock), .Q(d_ff_6_q));  // open: nQ
  D_FF d_ff_7 (.D(and_2_out), .C(clock), .Q(d_ff_7_q));  // open: nQ
  D_FF d_ff_8 (.D(d_ff_2_nq), .C(clock), .Q(d_ff_8_q));  // open: nQ
  D_FF d_ff_9 (.D(and_3_out), .C(clock), .Q(d_ff_9_q));  // open: nQ
  D_FF d_ff_10 (.D(d_ff_3_nq), .C(clock), .Q(d_ff_10_q));  // open: nQ
  or or_2 (or_2_out, MoneyChange, reset);
  and and_4 (Add5, d_ff_5_q, d_ff_6_q);
  and and_5 (Add10, d_ff_7_q, d_ff_8_q);
  and and_6 (Add20, d_ff_9_q, d_ff_10_q);
  Multiplexer #(.Bits(6)) multiplexer_4 (.sel(or_2_out), .in_0(d_ff_4_q), .in_1({6{1'b0}}), .out(Balance));
  Div #(.Bits(6)) C20 (.a(d_ff_4_q), .b(6'b010100), .q(C20_q), .r(C20_r));
  Div #(.Bits(6)) C10 (.a(C20_r), .b(6'b001010), .q(C10_q), .r(C10_r));
  Div #(.Bits(6)) C5 (.a(C10_r), .b(6'b000101), .q(C5_q));  // open: r
  Multiplexer #(.Bits(6)) multiplexer_5 (.sel(reset), .in_0(C20_q), .in_1({6{1'b0}}), .out(multiplexer_5_out));
  Multiplexer #(.Bits(6)) multiplexer_6 (.sel(reset), .in_0(C10_q), .in_1({6{1'b0}}), .out(multiplexer_6_out));
  Multiplexer #(.Bits(6)) multiplexer_7 (.sel(reset), .in_0(C5_q), .in_1({6{1'b0}}), .out(multiplexer_7_out));
  Comparator #(.Bits(6)) Tea (.a(Balance), .b(6'b010011), .gt(Tea_gt));  // open: eq, lt
  Comparator #(.Bits(6)) Coffee (.a(Balance), .b(6'b011000), .gt(Coffee_gt));  // open: eq, lt
  D_FF #(.Bits(6)) d_ff_11 (.D(multiplexer_5_out), .C(or_2_out), .Q({d_ff_11_q, Change20}));  // open: nQ
  D_FF #(.Bits(6)) d_ff_12 (.D(multiplexer_6_out), .C(or_2_out), .Q({d_ff_12_q, Change10}));  // open: nQ
  D_FF #(.Bits(6)) d_ff_13 (.D(multiplexer_7_out), .C(or_2_out), .Q({d_ff_13_q, Change5}));  // open: nQ
  and and_7 (and_7_out, Tea_gt, Ptea, ~CoffeeOut, ~TeaOut);  // And
  and and_8 (and_8_out, Coffee_gt, Pcoffee, ~CoffeeOut, ~TeaOut);  // And
  D_FF d_ff_14 (.D(and_7_out), .C(clock), .nQ(d_ff_14_nq));  // open: Q
  D_FF d_ff_15 (.D(and_8_out), .C(clock), .nQ(d_ff_15_nq));  // open: Q
  D_FF d_ff_16 (.D(and_7_out), .C(clock), .Q(d_ff_16_q));  // open: nQ
  D_FF d_ff_17 (.D(d_ff_14_nq), .C(clock), .Q(d_ff_17_q));  // open: nQ
  D_FF d_ff_18 (.D(and_8_out), .C(clock), .Q(d_ff_18_q));  // open: nQ
  D_FF d_ff_19 (.D(d_ff_15_nq), .C(clock), .Q(d_ff_19_q));  // open: nQ
  and and_9 (BuyTea, d_ff_16_q, d_ff_17_q);
  and and_10 (BuyCoffee, d_ff_18_q, d_ff_19_q);
  D_FF d_ff_20 (.D(Pchange), .C(clock), .Q(d_ff_20_q));  // open: nQ
  D_FF d_ff_21 (.D(Pnext), .C(clock), .Q(d_ff_21_q));  // open: nQ
  or or_3 (or_3_out, reset, NextDrink, MoneyChange);
  D_FF d_ff_22 (.D(d_ff_20_q), .C(clock), .nQ(d_ff_22_nq));  // open: Q
  D_FF d_ff_23 (.D(d_ff_21_q), .C(clock), .nQ(d_ff_23_nq));  // open: Q
  RS_FF_AS rs_ff_as_1 (.S(BuyTea), .R(or_3_out), .Q(rs_ff_as_1_q));  // open: nQ
  RS_FF_AS rs_ff_as_2 (.S(BuyCoffee), .R(or_3_out), .Q(rs_ff_as_2_q));  // open: nQ
  D_FF d_ff_24 (.D(d_ff_20_q), .C(clock), .Q(d_ff_24_q));  // open: nQ
  D_FF d_ff_25 (.D(d_ff_22_nq), .C(clock), .Q(d_ff_25_q));  // open: nQ
  D_FF d_ff_26 (.D(d_ff_21_q), .C(clock), .Q(d_ff_26_q));  // open: nQ
  D_FF d_ff_27 (.D(d_ff_23_nq), .C(clock), .Q(d_ff_27_q));  // open: nQ
  D_FF d_ff_28 (.D(rs_ff_as_1_q), .C(clock), .Q(TeaOut));  // open: nQ
  D_FF d_ff_29 (.D(rs_ff_as_2_q), .C(clock), .Q(CoffeeOut));  // open: nQ
  and and_11 (MoneyChange, d_ff_24_q, d_ff_25_q);
  and and_12 (NextDrink, d_ff_26_q, d_ff_27_q);
endmodule
