// Digital circuit T-FF by J-K FF.dig as structural Verilog
module T_FF_by_J_K_FF (
  input  T,
  input  Cock,
  output Q,
  output Q_2
);

  JK_FF jk_ff_1 (.J(T), .C(Cock), .K(T), .Q(Q), .nQ(Q_2));
endmodule
