// Digital circuit Midterm.dig as structural Verilog
module Midterm (
  input  A,
  input  B,
  input  [2:0] S,
  output F,
  output Cout
);

  wire and_1_out, and_2_out, and_3_out, and_4_out, or_1_out, xor_1_out;

  xor xor_1 (xor_1_out, A, B);
  or or_1 (or_1_out, A, B);
  and and_1 (and_1_out, A, B);
  and and_2 (and_2_out, A, ~B);  // And
  and and_3 (and_3_out, ~A, B);  // And
  and and_4 (and_4_out, A, B);
  Multiplexer #(.Selector_Bits(3)) multiplexer_1 (
    .sel(S), .in_0(1'b0), .in_1(xor_1_out), .in_2(xor_1_out), .in_3(xor_1_out), .in_4(xor_1_out),
    .in_5(or_1_out), .in_6(and_1_out), .in_7(1'b1), .out(F));
  Multiplexer #(.Selector_Bits(3)) multiplexer_2 (
    .sel(S), .in_0(1'b0), .in_1(and_2_out), .in_2(and_3_out), .in_3(and_4_out), .in_4(1'b0), .in_5(1'b0),
    .in_6(1'b0), .in_7(1'b0), .out(Cout));
endmodule
