// Digital circuit NAND, NOR test.dig as structural Verilog
module NAND__NOR_test (
  input  D,
  input  C,
  input  B,
  input  A,
  output out_5,
  output out_6,
  output out_7,
  output NOR,
  output NOR_2,
  output NOR_3,
  output NOR_4,
  output NAND
);

  wire and_1_out, and_2_out, nand_1_out, nand_2_out, nor_1_out, nor_2_out, not_1_out, not_2_out, not_3_out,
       not_4_out, not_5_out, not_6_out, or_1_out, or_2_out, or_3_out, or_4_out;

  and and_1 (and_1_out, D, C);
  and and_2 (and_2_out, B, A);
  nand nand_1 (nand_1_out, D, C);
  nand nand_2 (nand_2_out, B, A);
  or or_1 (or_1_out, D, C);
  or or_2 (or_2_out, B, A);
  nor nor_1 (nor_1_out, D, C);
  nor u_nor_2 (nor_2_out, B, A);
  nor u_nor_3 (NOR_2, D, C, B, A);
  and and_3 (NOR_3, ~D, ~C, ~B, ~A);  // And
  or or_3 (or_3_out, ~A, ~B);  // Or
  or or_4 (or_4_out, ~C, ~D);  // Or
  or or_5 (out_6, ~A, ~B, ~C, ~D);  // Or
  not not_1 (not_1_out, or_3_out);
  not not_2 (not_2_out, or_4_out);
  not not_3 (not_3_out, nand_1_out);
  not not_4 (not_4_out, nand_2_out);
  nor u_nor_4 (NOR, or_1_out, or_2_out);
  not not_5 (not_5_out, nor_1_out);
  not not_6 (not_6_out, nor_2_out);
  or or_6 (out_5, ~not_1_out, ~not_2_out);  // Or
  nand nand_3 (out_7, and_1_out, and_2_out);
  nand nand_4 (NAND, not_3_out, not_4_out);
  nor nor_5 (NOR_4, not_5_out, not_6_out);
endmodule
