// Digital circuit counter_test.dig as structural Verilog
module counter_test (
  input  clk,
  output [3:0] out_2
);

  wire _74163_1_pin1, and_1_out;

  _74163 _74163_1 (
    .pin1(_74163_1_pin1), .pin2(clk), .pin3(1'b0), .pin4(1'b0), .pin5(1'b0), .pin6(1'b0), .pin7(1'b1),
    .pin8(1'b0), .pin9(1'b1), .pin10(1'b1), .pin11(out_2[3]), .pin12(out_2[2]), .pin13(out_2[1]),
    .pin14(out_2[0]), .pin16(1'b1));  // open: pin15
  and and_1 (and_1_out, ~out_2[0], out_2[1], out_2[2], ~out_2[3]);  // And
  not not_1 (_74163_1_pin1, and_1_out);
endmodule
