// Digital circuit ripple counter from T ff.dig as structural Verilog
module ripple_counter_from_T_ff (
  input  clk,
  output [5:0] out_2
);

  wire and_1_out, and_2_out, or_1_out, or_2_out, or_3_out, or_4_out;

  and and_1 (and_1_out, out_2[5], out_2[4], out_2[3], ~out_2[2], out_2[1], out_2[0]);  // And
  T_FF t_ff_1 (.T(1'b1), .C(~clk), .Q(out_2[0]));  // open: nQ
  or or_1 (or_1_out, out_2[0], and_1_out);
  T_FF t_ff_2 (.T(1'b1), .C(~or_1_out), .Q(out_2[1]));  // open: nQ
  and and_2 (and_2_out, out_2[1], ~and_1_out);  // And
  T_FF t_ff_3 (.T(1'b1), .C(~and_2_out), .Q(out_2[2]));  // open: nQ
  or or_2 (or_2_out, and_1_out, out_2[2]);
  T_FF t_ff_4 (.T(1'b1), .C(~or_2_out), .Q(out_2[3]));  // open: nQ
  or or_3 (or_3_out, out_2[3], and_1_out);
  T_FF t_ff_5 (.T(1'b1), .C(~or_3_out), .Q(out_2[4]));  // open: nQ
  or or_4 (or_4_out, out_2[4], and_1_out);
  T_FF t_ff_6 (.T(1'b1), .C(~or_4_out), .Q(out_2[5]));  // open: nQ

  // Other names for the same wires on the sheet: A = out_2[5]; B = out_2[4]; C = out_2[3]; D = out_2[2]; E = out_2[1];
  //   F = out_2[0]
endmodule
